# Fritzing sketch sơ đồ nguyên lý (saved by Fritzing 0.9.9b)

parts:
  R1 = Rotary Potentiometer (Large) [maximum_resistance=100kΩ package=THT]
  U1 = ESP32-38PinWide [part_number=ESP32-38PinWide]
  M1 = DC Motor
  VCC1 = Battery
  S1 = H-Bridge with L298N
  J1 = Basic Servo

nets:
  N1: R1.leg1, U1.VIN
  N2: R1.wiper, U1.GPIO13
  GND: R1.leg2, U1.GND, S1.GND, J1.gnd
  N3: U1.GPIO27, S1.ENA
  N4: U1.GPIO14, S1.IN1
  N5: U1.GPIO12, S1.IN2
  N6: M1.pin_1, S1.M1-02
  N7: M1.pin_2, S1.M1-01
  N8: VCC1.-, S1.12V

notes:
  esp32------- biến trở
  gpio13 chân giữa
  gpio12 - in2
  gpio14 - in1
  gpio27 - ena
  chung gnd
  gpio 26 - servo

custom parts:
  ESP32-38PinWide: Generic 38-Pin ESP32 with wide format (only access to one side of pins on a breadboard) based on Stephen Lilley's HiLetgo ESP-WROOM-32 ESP32 ESP-32S Development Board.
  H-Bridge with L298N: h-bridge
